# Fritzing sketch Tag Reader Schematics v3.1 (saved by Fritzing 0.9.4)

parts:
  Part1 = PN532 Elechouse RFID NFC Module V3
  WeMos_D1_Mini1 = WeMos D1 Mini
  J1 = Piezo Speaker
  RGB_SMD_LED1 = SMD RGB LED (WS2812) [package=5050]

nets:
  N1: Part1.GND, WeMos_D1_Mini1.G, J1.pin1, RGB_SMD_LED1.DOut
  VCC: Part1.VCC, WeMos_D1_Mini1.5V, RGB_SMD_LED1.VCC
  N2: Part1.SCL, WeMos_D1_Mini1.D2
  N3: WeMos_D1_Mini1.D7, J1.pin2
  N4: WeMos_D1_Mini1.D8, RGB_SMD_LED1.DIn

custom parts:
  PN532 Elechouse RFID NFC Module V3: NFC is a popular technology in recent years. We often heard this work while smart phone company such as Samsung or HTC introduces their latest high-end phones. Almost all the high-end phone in the market support NFC. Near field communication (NFC) is a set of standards for smart phones and similar devices to establish radio communication with each other by touching them together or bringing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
