# Fritzing sketch Tag Reader Schematics (saved by Fritzing 0.9.5d)

parts:
  Part1 = PN532 Elechouse RFID NFC Module V3
  WeMos_D1_Mini1 = WeMos D1 Mini
  LED1 = prefix0000
  J1 = Piezo Speaker

nets:
  N1: Part1.GND, WeMos_D1_Mini1.G, LED1.connector3, J1.pin1
  VCC: Part1.VCC, WeMos_D1_Mini1.5V, LED1.connector1
  N2: Part1.SCL, WeMos_D1_Mini1.D1
  N3: WeMos_D1_Mini1.D7, J1.pin2
  N4: WeMos_D1_Mini1.D8, LED1.connector2

custom parts:
  PN532 Elechouse RFID NFC Module V3: NFC is a popular technology in recent years. We often heard this work while smart phone company such as Samsung or HTC introduces their latest high-end phones. Almost all the high-end phone in the market support NFC. Near field communication (NFC) is a set of standards for smart phones and similar devices to establish radio communication with each other by touching them together or bringing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
